# Fritzing sketch FC New 2-layer dedicated (saved by Fritzing 0.9.4)
circuit board: 11.4914cm x 5.88821cm
breadboards: 1

parts:
  S7 = male pin header, 3 pins [form="♂ (male)"]
  S8 = male pin header, 3 pins [form="♂ (male)"]
  Diode = Rectifier Diode [part_number="1N4148 " package="300 mil [THT]"]
  Resistor = Resistor [tolerance=±5% resistance=10k package=THT]
  Sensor = male pin header, 3 pins [form="♂ (male)"]
  Servo = male pin header, 3 pins [form="♂ (male)"]
  T2_R2_Bz-_LED = molex pin header, 4 pins [form=molex]
  DA_CL_T1_R1 = molex pin header, 4 pins [form=molex]
  T4_R4_T3_R3 = molex pin header, 4 pins [form=molex]
  3V_4V_T6_R6 = molex pin header, 4 pins [form=molex]
  S4_S3_S2_S1 = molex pin header, 4 pins [form=molex]
  S8_S7_S6_S5 = molex pin header, 4 pins [form=molex]
  L1 = male pin header, 4 pins [form="♂ (male)"]
  L6 = male pin header, 4 pins [form="♂ (male)"]
  L2 = male pin header, 4 pins [form="♂ (male)"]
  L5 = male pin header, 4 pins [form="♂ (male)"]
  L4 = male pin header, 4 pins [form="♂ (male)"]
  S3 = male pin header, 4 pins [form="♂ (male)"]
  S6 = male pin header, 4 pins [form="♂ (male)"]
  S4 = male pin header, 4 pins [form="♂ (male)"]
  S2 = male pin header, 4 pins [form="♂ (male)"]
  S1 = male pin header, 4 pins [form="♂ (male)"]
  S5 = male pin header, 4 pins [form="♂ (male)"]
  Buzzer = female pin header, 5 pins [form="♀ (female)"]
  VTX-HV = male pin header, 6 pins [form="♂ (male)"]
  Camera3 = female pin header, 4 pins [form="♀ (female)"]
  C2_C1_G_5V = molex pin header, 4 pins [form=molex]
  G_VTX_GND_Vbat = molex pin header, 4 pins [form=molex]
  Bluetooth = male pin header, 6 pins [form="♂ (male)"]
  OLED = male pin header, 4 pins [form="♂ (male)"]
  BT_En = male pin header, 3 pins [form="♂ (male)"]
  GPS_Puck = male pin header, 6 pins [form="♂ (male)"]
  GND_5V = molex pin header, 2 pins [form=molex]
  Camera1 = male pin header, 6 pins [form="♂ (male)"]
  L0 = male pin header, 4 pins [form="♂ (male)"]
  L3 = male pin header, 4 pins [form="♂ (male)"]
  Camera2 = male pin header, 4 pins [form="♂ (male)"]
  Range = male pin header, 6 pins [form="♂ (male)"]
  3V = male pin header, 2 pins [form="♂ (male)"]
  4V = male pin header, 2 pins [form="♂ (male)"]
  5V = male pin header, 2 pins [form="♂ (male)"]

nets:
  N1: S7.pin1, S8.pin1, Sensor.pin1, Servo.pin1, L1.pin4, L6.pin4, L2.pin4, L5.pin4, L4.pin4, S3.pin1, S6.pin1, S4.pin1, S2.pin1, S1.pin1, S5.pin1, Buzzer.pin3, Bluetooth.pin4, OLED.pin1, BT_En.pin3, GPS_Puck.pin1, GND_5V.pin1, L0.pin4, L3.pin4, Range.pin2, 3V.pin1, 4V.pin1, 5V.pin1
  N2: S7.pin2, S8.pin2, L1.pin2, L2.pin2, L5.pin2, S2.pin2, S1.pin2, S5.pin2, Bluetooth.pin5, BT_En.pin1, GPS_Puck.pin2, GND_5V.pin2, Range.pin1
  N3: S7.pin3, S8_S7_S6_S5.pin2
  N4: S8.pin3, S8_S7_S6_S5.pin1
  N5: Diode.cathode, Servo.pin3
  N6: Diode.anode, Resistor.Pin_1, T2_R2_Bz-_LED.pin2
  N7: Resistor.Pin_0, Sensor.pin3
  N8: Sensor.pin2, Servo.pin2, 3V_4V_T6_R6.pin2, Buzzer.pin2, OLED.pin2, L0.pin2, 4V.pin2
  N9: T2_R2_Bz-_LED.pin3, Buzzer.pin4
  N10: T2_R2_Bz-_LED.pin4, L0.pin3
  N11: DA_CL_T1_R1.pin1, OLED.pin4, GPS_Puck.pin6, Range.pin4
  N12: DA_CL_T1_R1.pin2, OLED.pin3, GPS_Puck.pin5, Range.pin3
  N13: DA_CL_T1_R1.pin3, GPS_Puck.pin4
  N14: DA_CL_T1_R1.pin4, GPS_Puck.pin3
  N15: T4_R4_T3_R3.pin1, Camera1.pin5
  N16: T4_R4_T3_R3.pin2, Camera1.pin6
  N17: T4_R4_T3_R3.pin3, Camera3.pin3
  N18: T4_R4_T3_R3.pin4, Camera3.pin4
  N19: 3V_4V_T6_R6.pin1, 3V.pin2
  N20: 3V_4V_T6_R6.pin3, Bluetooth.pin2
  N21: 3V_4V_T6_R6.pin4, Bluetooth.pin3
  N22: S4_S3_S2_S1.pin1, S4.pin3
  N23: S4_S3_S2_S1.pin2, S3.pin3
  N24: S4_S3_S2_S1.pin3, S2.pin3, S2.pin4
  N25: S4_S3_S2_S1.pin4, S1.pin3
  N26: S8_S7_S6_S5.pin3, S6.pin3
  N27: S8_S7_S6_S5.pin4, S5.pin3
  N28: L1.pin1, L2.pin3
  N29: L1.pin3, L0.pin1
  N30: L6.pin2, S6.pin2
  N31: L6.pin3, L5.pin1
  N32: L2.pin1, L3.pin3
  N33: L5.pin3, L4.pin1
  N34: L4.pin2, S4.pin2, 5V.pin2
  N35: L4.pin3, L3.pin1
  N36: S3.pin2, L3.pin2
  N37: VTX-HV.pin1, G_VTX_GND_Vbat.pin4
  N38: VTX-HV.pin2, G_VTX_GND_Vbat.pin3
  N39: VTX-HV.pin4, G_VTX_GND_Vbat.pin1
  N40: VTX-HV.pin5, G_VTX_GND_Vbat.pin2
  N41: VTX-HV.pin6, Camera1.pin4, Camera2.pin4
  N42: C2_C1_G_5V.pin1, Camera2.pin3
  N43: C2_C1_G_5V.pin2, Camera1.pin3
  N44: C2_C1_G_5V.pin3, Camera1.pin2, Camera2.pin2
  N45: C2_C1_G_5V.pin4, Camera1.pin1, Camera2.pin1
  N46: Bluetooth.pin6, BT_En.pin2

notes:
  by Neuroplant '20
  GB tilt
  Hook
  Matek F722-SE
  U1 - GPS
  U2 - IBUS/Telemetrie
  U3 - VTX
  I2C - Compass
  I2C - OLED Screen
  I2C -Range Sensor
  U4 - Camera1
  U6 - Bluetooth/MSP
  U2 - Receiver (IBUS)/ FlySky FS-IA10b
  U3 - VTX/ Matek VTX-VH
  U4 - Camera1 (with UART Control)
  U6 - Bluetooth/MSP H-08
  I2C - OLED/ SSD1306 12864
  I2C - Range Sensor/ GY-VL53L0XV2
  GND
  GND 4V5 CL DA
  5V GND CL DA GP XS
  GND 5V TX1 RX1 CL DA
  5V GND C1 Aux Rx4 TX4
  5V GND C2 Aux
  GND 4V5 S
  Dout 5V Din GND
  GND 5V S
  Hi En Lo
  Bz- GND 4V5
  RX6 TX6 GND 5V PW
  Aux VTX G     GND Vbat
  TX3 RX3
